# Fritzing sketch 1 - PiscarLed (saved by Fritzing 0.9.3b)
breadboards: 1

parts:
  Componente1 = Arduino Nano (Rev3.0)
  R1 = Resistor [tolerance=±5% resistance=220 package=THT]
  LED1 = LED - 5mm [color="Red (633nm)" package="5 mm [THT]"]

nets:
  N1: Componente1.GND, LED1.anode
  N2: Componente1.D13/SCK, R1.Pin_1
  N3: R1.Pin_0, LED1.cathode
