# Fritzing sketch 2 - Acionando Botao (saved by Fritzing 0.9.3b)
perfboards: 1
breadboards: 1

parts:
  S1 = Pushbutton [package="[THT]"]
  R1 = Resistor [tolerance=±5% resistance=10k package=THT]  # not connected
  Componente1 = Arduino Nano (Rev3.0)  # not connected

nets:
  N1: S1.Pin_1, S1.Pin_2
  N2: S1.Pin_3, S1.Pin_4
