# Fritzing sketch 3 - FazendoLeituraControle (saved by Fritzing 0.9.3b)
breadboards: 1

parts:
  TCRT1 = TCRT5000 sensor module [part_number=151608]  # not connected
  Componente1 = Arduino Nano (Rev3.0)
  R1 = Resistor [tolerance=±5% resistance=10k package=THT]
  R2 = Resistor [tolerance=±5% resistance=330 package=THT]

nets:
  N1: Componente1.GND, R1.Pin_0
  N2: Componente1.5V, R2.Pin_0

custom parts:
  TCRT5000 sensor module: breakout board with TCRT5000
