# Fritzing sketch 4 - Enviando Sinais IR (saved by Fritzing 0.9.3b)
breadboards: 1
perfboards: 1

parts:
  Componente1 = Arduino Nano (Rev3.0)
  S1 = Pushbutton [package="[THT]"]
  R1 = Resistor [tolerance=±5% resistance=10k package=THT]
  LED1 = LED - 5mm [color="Red (633nm)" package="5 mm [THT]"]
  R2 = Resistor [tolerance=±5% resistance=100 package=THT]

nets:
  N1: Componente1.GND, R1.Pin_1, LED1.anode
  N2: Componente1.D3, LED1.cathode, R2.Pin_1
  N3: Componente1.5V, R2.Pin_0
  N4: S1.Pin_1, S1.Pin_2
  N5: S1.Pin_3, S1.Pin_4
