# Fritzing sketch 5 - Carregando o Bluetooth (saved by Fritzing 0.9.3b)
breadboards: 1
perfboards: 1

parts:
  S1 = Pushbutton [package="[THT]"]
  R2 = Resistor [tolerance=±5% resistance=1.5k package=THT]
  R3 = Resistor [tolerance=±5% resistance=2.2k package=THT]
  R1 = Resistor [tolerance=±5% resistance=10k package=THT]  # not connected
  Componente1 = Arduino Nano (Rev3.0)
  U3 = mystery part, 4 pins [chip_label=HC-05]

nets:
  N1: S1.Pin_1, S1.Pin_2
  N2: S1.Pin_3, S1.Pin_4
  N3: R2.Pin_1, R3.Pin_0
  N4: R3.Pin_1, Componente1.D1/TX
  N5: Componente1.D0/RX, U3.pin2
  N6: Componente1.GND, U3.pin3
  N7: Componente1.5V, U3.pin4
